// Logisim project ALU.circ as structural Verilog: 1 circuit, main circuit main
module main (
  input  [15:0] B,
  input  [15:0] A,
  input  [3:0] ALU_signal,
  output ZERO_flag,
  output [15:0] RESULT,
  output Over_flow
);

  wire adder_1_cout, comparator_1_lt, comparator_2_lt, subtractor_1_bout, xor_2_out, xor_3_out;
  wire [15:0] adder_1_out, and_1_out, bit_extender_1_out, bit_extender_2_out, not_1_out, or_1_out,
       shifter_1_out, shifter_2_out, shifter_3_out, shifter_4_out, subtractor_1_out, xor_1_out;

  Comparator #(.width(16), .mode("unsigned")) comparator_1 (.a(A), .b(B), .lt(comparator_1_lt));  // open: gt, eq
  Comparator #(.width(16)) comparator_2 (.a(A), .b(B), .lt(comparator_2_lt));  // open: gt, eq
  assign and_1_out = A & B;  // AND_Gate and_1, 16 bits wide
  assign or_1_out = A | B;  // OR_Gate or_1, 16 bits wide
  assign xor_1_out = A ^ B;  // XOR_Gate xor_1, 16 bits wide
  Adder #(.width(16)) adder_1 (.a(A), .b(B), .out(adder_1_out), .cout(adder_1_cout));  // open: cin
  Subtractor #(.width(16)) subtractor_1 (.a(A), .b(B), .out(subtractor_1_out), .bout(subtractor_1_bout));  // open: bin
  assign not_1_out = ~or_1_out;  // NOT_Gate not_1, 16 bits wide
  Comparator #(.width(16)) comparator_3 (.a(A), .b(B), .eq(ZERO_flag));  // open: gt, lt
  Shifter #(.width(16)) shifter_1 (.in(A), .\dist (B[3:0]), .out(shifter_1_out));
  Shifter #(.width(16), .shift("lr")) shifter_2 (.in(A), .\dist (B[3:0]), .out(shifter_2_out));
  Shifter #(.width(16), .shift("ar")) shifter_3 (.in(A), .\dist (B[3:0]), .out(shifter_3_out));
  Shifter #(.width(16), .shift("rr")) shifter_4 (.in(A), .\dist (B[3:0]), .out(shifter_4_out));
  xor xor_2 (xor_2_out, adder_1_out[15], adder_1_cout);
  xor xor_3 (xor_3_out, subtractor_1_out[15], subtractor_1_bout);
  or or_2 (Over_flow, xor_2_out, xor_3_out);
  assign bit_extender_1_out = {{15{1'b0}}, comparator_2_lt};  // Bit_Extender bit_extender_1
  assign bit_extender_2_out = {{15{1'b0}}, comparator_1_lt};  // Bit_Extender bit_extender_2
  Multiplexer #(.select(4), .width(16), .enable("false")) multiplexer_1 (
    .in0(shifter_1_out), .in1(shifter_2_out), .in2(shifter_3_out), .in3(shifter_4_out), .in4(and_1_out),
    .in5(not_1_out), .in6(or_1_out), .in7(xor_1_out), .in8(adder_1_out), .in9(subtractor_1_out),
    .in10(bit_extender_1_out), .in11(bit_extender_2_out), .out(RESULT), .sel(ALU_signal));  // open: in12, in13, in14, in15

  // Notes on the sheet:
  //   First comparator : for check SLTU
  //   Second comparator :for check SLT,BEQ,BLT,BGE
  //   Shift amont 0:4
  //   SLL 0
  //   SRL 1
  //   SRA 2
  //   ROR 3
  //   AND 4
  //   NOR 5
  //   OR 6
  //   XOR 7
  //   ADD 8
  //   SUB 9
  //   SLT 10
  //   SLTU11
endmodule
