// Logisim project Comparator.circ as structural Verilog: 1 circuit, main circuit main
module main (
  input  [4:0] OP_code_1,
  input  [15:0] Read_data_a_1,
  input  [15:0] Read_data_b_1,
  output Taken
);

  wire BEQ_out, BGE_out, BLT_out, BNE_out, comparator_1_eq, comparator_1_lt;

  Comparator #(.width(16)) comparator_1 (
    .a(Read_data_a_1), .b(Read_data_b_1), .eq(comparator_1_eq), .lt(comparator_1_lt));  // open: gt
  and BEQ (BEQ_out, ~OP_code_1[4], OP_code_1[3], OP_code_1[2], OP_code_1[1], ~OP_code_1[0], comparator_1_eq);  // AND_Gate
  and BNE (BNE_out, ~OP_code_1[4], OP_code_1[3], OP_code_1[2], OP_code_1[1], OP_code_1[0], ~comparator_1_eq);  // AND_Gate
  or or_1 (Taken, BEQ_out, BNE_out, BLT_out, BGE_out);
  and BLT (BLT_out, OP_code_1[4], ~OP_code_1[3], ~OP_code_1[2], ~OP_code_1[1], ~OP_code_1[0], comparator_1_lt);  // AND_Gate
  and BGE (BGE_out, OP_code_1[4], ~OP_code_1[3], ~OP_code_1[2], ~OP_code_1[1], OP_code_1[0], ~comparator_1_lt);  // AND_Gate

  // Other names for the same wires on the sheet: BIT0 = OP_code_1[0]; BIT1 = OP_code_1[1]; BIT2 = OP_code_1[2];
  //   BIT3 = OP_code_1[3]; BIT4 = OP_code_1[4]

  // Notes on the sheet:
  //   checks if a branch is taken or not
  //   is taken
  //   Op code is splitted into 5 bits to know which
endmodule
