// Logisim project EX-MEM.circ as structural Verilog: 1 circuit, main circuit main
module main (
  input  [15:0] PC_1_2,
  input  [15:0] Result_of_ALU_2,
  input  [2:0] RW_2,
  input  [15:0] LUI_result_2,
  input  [15:0] BUSB_2,
  input  [15:0] BUSA_2,
  input  MemWrite_2,
  input  MemRead_2,
  input  REG_write_2,
  input  [1:0] MemtoReg_2,
  input  CLOCK,
  output [15:0] PC_1_3,
  output [15:0] Result_of_ALU_3,
  output [2:0] RW_3,
  output [15:0] LUI_result_3,
  output [15:0] BUSB_3,
  output [15:0] BUSA_3,
  output MemWrite_3,
  output MemRead_3,
  output REG_write_3,
  output [1:0] MemtoReg_3
);

  Register #(.width(16)) register_1 (.D(PC_1_2), .en(CLOCK), .Q(PC_1_3), .clk(CLOCK));  // open: clr
  Register #(.width(16)) register_2 (.D(Result_of_ALU_2), .en(CLOCK), .Q(Result_of_ALU_3), .clk(CLOCK));  // open: clr
  Register #(.width(3)) register_3 (.D(RW_2), .en(CLOCK), .Q(RW_3), .clk(CLOCK));  // open: clr
  Register #(.width(16)) register_4 (.D(LUI_result_2), .en(CLOCK), .Q(LUI_result_3), .clk(CLOCK));  // open: clr
  Register #(.width(16)) register_5 (.D(BUSB_2), .en(CLOCK), .Q(BUSB_3), .clk(CLOCK));  // open: clr
  Register #(.width(16)) register_6 (.D(BUSA_2), .en(CLOCK), .Q(BUSA_3), .clk(CLOCK));  // open: clr
  Register #(.width(1)) register_7 (.D(MemWrite_2), .en(CLOCK), .Q(MemWrite_3), .clk(CLOCK));  // open: clr
  Register #(.width(1)) register_8 (.D(MemRead_2), .en(CLOCK), .Q(MemRead_3), .clk(CLOCK));  // open: clr
  Register #(.width(1)) register_9 (.D(REG_write_2), .en(CLOCK), .Q(REG_write_3), .clk(CLOCK));  // open: clr
  Register #(.width(2)) register_10 (.D(MemtoReg_2), .en(CLOCK), .Q(MemtoReg_3), .clk(CLOCK));  // open: clr
endmodule
