// Logisim project Hazard Detect Forward and Stall.circ as structural Verilog: 1 circuit, main circuit main
module main (
  input  [2:0] RW_2,
  input  REG_write_2,
  input  [2:0] Rs,
  input  [2:0] RW_3,
  input  REG_write_3,
  input  [2:0] Rt,
  input  REG_write_4,
  input  LUI,
  input  [2:0] RW_4,
  input  MemRead_2,
  input  [4:0] OP_code_1,
  output Stall,
  output [2:0] ForwardB,
  output [2:0] ForwardA,
  output ForwardC,
  output ForwardD
);

  wire and_2_out, and_3_out, and_4_out, and_5_out, and_8_out, and_9_out, and_10_out, and_11_out, BEQ, BGE,
       BLT, BNE, comparator_1_eq, comparator_2_eq, comparator_3_eq, comparator_4_eq, comparator_5_eq,
       comparator_6_eq, comparator_7_eq, comparator_8_eq, comparator_9_eq, comparator_10_eq,
       comparator_11_eq, comparator_12_eq, comparator_13_eq, comparator_14_eq, comparator_15_eq,
       comparator_16_eq, comparator_17_eq, comparator_18_eq, comparator_19_eq, comparator_20_eq, nor_1_out,
       nor_2_out, or_1_out, or_2_out, or_3_out, or_4_out;

  or or_1 (or_1_out, BEQ, BNE, BLT, BGE);
  Comparator #(.width(3), .mode("unsigned")) comparator_1 (.a(RW_3), .b(3'b000), .eq(comparator_1_eq));  // open: gt, lt
  Comparator #(.width(3), .mode("unsigned")) comparator_2 (.a(RW_3), .b(Rs), .eq(comparator_2_eq));  // open: gt, lt
  Comparator #(.width(3), .mode("unsigned")) comparator_3 (.a(Rs), .b(3'b000), .eq(comparator_3_eq));  // open: gt, lt
  Comparator #(.width(3), .mode("unsigned")) comparator_4 (.a(Rs), .b(RW_4), .eq(comparator_4_eq));  // open: gt, lt
  Comparator #(.width(3), .mode("unsigned")) comparator_5 (.a(Rs), .b(3'b000), .eq(comparator_5_eq));  // open: gt, lt
  Comparator #(.width(3), .mode("unsigned")) comparator_6 (.a(Rs), .b(RW_3), .eq(comparator_6_eq));  // open: gt, lt
  Comparator #(.width(3), .mode("unsigned")) comparator_7 (.a(Rs), .b(3'b000), .eq(comparator_7_eq));  // open: gt, lt
  Comparator #(.width(3), .mode("unsigned")) comparator_8 (.a(Rs), .b(RW_2), .eq(comparator_8_eq));  // open: gt, lt
  Comparator #(.width(3), .mode("unsigned")) comparator_9 (.a(Rs), .b(3'b000), .eq(comparator_9_eq));  // open: gt, lt
  Comparator #(.width(3), .mode("unsigned")) comparator_10 (.a(Rs), .b(RW_2), .eq(comparator_10_eq));  // open: gt, lt
  and and_1 (ForwardC, or_1_out, ~comparator_1_eq, comparator_2_eq);  // AND_Gate
  and and_2 (and_2_out, ~comparator_3_eq, comparator_4_eq, REG_write_4);  // AND_Gate
  and and_3 (and_3_out, ~comparator_5_eq, comparator_6_eq, REG_write_3);  // AND_Gate
  and and_4 (and_4_out, ~comparator_7_eq, comparator_8_eq, REG_write_2);  // AND_Gate
  and and_5 (and_5_out, ~comparator_9_eq, comparator_10_eq, REG_write_2, LUI);  // AND_Gate
  nor nor_1 (nor_1_out, and_2_out, and_3_out, and_4_out, and_5_out);
  Priority_Encoder priority_encoder_1 (
    .in0(nor_1_out), .in1(and_2_out), .in2(and_3_out), .in3(and_4_out), .in4(and_5_out), .out(ForwardA));  // open: in5, in6, in7, en_in, gs, en_out
  Comparator #(.width(3), .mode("unsigned")) comparator_11 (
    .a(RW_3), .b(3'b000), .eq(comparator_11_eq));  // open: gt, lt
  Comparator #(.width(3), .mode("unsigned")) comparator_12 (.a(RW_3), .b(Rt), .eq(comparator_12_eq));  // open: gt, lt
  or or_2 (or_2_out, ForwardA[0], ForwardB[0]);
  or or_3 (or_3_out, MemRead_2, LUI);
  or or_4 (or_4_out, BEQ, BNE, BLT, BGE);
  and and_6 (Stall, or_2_out, or_3_out);
  and and_7 (ForwardD, or_4_out, ~comparator_11_eq, comparator_12_eq);  // AND_Gate
  Comparator #(.width(3), .mode("unsigned")) comparator_13 (.a(Rt), .b(3'b000), .eq(comparator_13_eq));  // open: gt, lt
  Comparator #(.width(3), .mode("unsigned")) comparator_14 (.a(Rt), .b(RW_4), .eq(comparator_14_eq));  // open: gt, lt
  Comparator #(.width(3), .mode("unsigned")) comparator_15 (.a(Rt), .b(3'b000), .eq(comparator_15_eq));  // open: gt, lt
  Comparator #(.width(3), .mode("unsigned")) comparator_16 (.a(Rt), .b(RW_3), .eq(comparator_16_eq));  // open: gt, lt
  Comparator #(.width(3), .mode("unsigned")) comparator_17 (.a(Rt), .b(3'b000), .eq(comparator_17_eq));  // open: gt, lt
  Comparator #(.width(3), .mode("unsigned")) comparator_18 (.a(Rt), .b(RW_2), .eq(comparator_18_eq));  // open: gt, lt
  Comparator #(.width(3), .mode("unsigned")) comparator_19 (.a(Rt), .b(3'b000), .eq(comparator_19_eq));  // open: gt, lt
  Comparator #(.width(3), .mode("unsigned")) comparator_20 (.a(Rt), .b(RW_2), .eq(comparator_20_eq));  // open: gt, lt
  and and_8 (and_8_out, ~comparator_13_eq, comparator_14_eq, REG_write_4);  // AND_Gate
  and and_9 (and_9_out, ~comparator_15_eq, comparator_16_eq, REG_write_3);  // AND_Gate
  and and_10 (and_10_out, ~comparator_17_eq, comparator_18_eq, REG_write_2);  // AND_Gate
  and and_11 (and_11_out, ~comparator_19_eq, comparator_20_eq, REG_write_2, LUI);  // AND_Gate
  Decoder #(.select(5), .enable("false")) decoder_1 (
    .out14(BEQ), .out15(BNE), .out16(BLT), .out17(BGE), .sel(OP_code_1));  // open: out0, out1, out2, out3, out4, out5, out6, out7, out8, out9, out10, out11, out12, out13, out18, out19, out20, out21, out22, out23, out24, out25, out26, out27, out28, out29, out30, out31
  nor nor_2 (nor_2_out, and_8_out, and_9_out, and_10_out, and_11_out);
  Priority_Encoder priority_encoder_2 (
    .in0(nor_2_out), .in1(and_8_out), .in2(and_9_out), .in3(and_10_out), .in4(and_11_out), .out(ForwardB));  // open: in5, in6, in7, en_in, gs, en_out

  // Notes on the sheet:
  //   encoder to generate the signal of forwardA mux 
  //   priority is taken into consideration
  //   MEM/WB
  //   EX/MEM
  //   ALU
  //   Result of Lui
  //   forwardC and forwardD are muxs used in the comparator 
  //   to detect branches
  //   if A=1, B=1
  //   First bit
  //   implementaion circuit of stall.
  //   and EX.memread =1 + LUI = 1
  //   MEM/WB
  //   EX/MEM
  //   ALU
  //   Result of Lui
  //   encoder to generate the signal of forwardB mux 
  //   priority is taken into consideration
endmodule
