// Logisim project ID-EX.circ as structural Verilog: 1 circuit, main circuit main
module main (
  input  [15:0] signed__Imm11__1,
  input  [15:0] PC_1_1,
  input  [15:0] BUSA_1,
  input  [15:0] BUSB_1,
  input  [2:0] RW_1,
  input  [15:0] signed__Imm5__1,
  input  [15:0] unsigned__Imm5__1,
  input  MemWrite_1,
  input  MemRead_1,
  input  [1:0] ALUSrc_1,
  input  REG_write_1,
  input  [1:0] MemtoReg_1,
  input  [3:0] Alu_Signal_1,
  input  LUI_0,
  input  Clock,
  output [15:0] signed__Imm11__1_2,
  output [15:0] PC_1_2,
  output [15:0] BUSA_2,
  output [15:0] BUSB_2,
  output [2:0] RW_2,
  output [15:0] signed__Imm5__2,
  output [15:0] unsigned__Imm5__2,
  output MemWrite_2,
  output MemRead_2,
  output [1:0] ALUSrc_2,
  output REG_write_2,
  output [1:0] MemtoReg_2,
  output [3:0] Alu_Signal_2,
  output LUI_1
);

  Register #(.width(16)) register_1 (
    .D(signed__Imm11__1), .en(Clock), .Q(signed__Imm11__1_2), .clk(Clock));  // open: clr
  Register #(.width(16)) register_2 (.D(PC_1_1), .en(Clock), .Q(PC_1_2), .clk(Clock));  // open: clr
  Register #(.width(16)) register_3 (.D(BUSA_1), .en(Clock), .Q(BUSA_2), .clk(Clock));  // open: clr
  Register #(.width(16)) register_4 (.D(BUSB_1), .en(Clock), .Q(BUSB_2), .clk(Clock));  // open: clr
  Register #(.width(3)) register_5 (.D(RW_1), .en(Clock), .Q(RW_2), .clk(Clock));  // open: clr
  Register #(.width(16)) register_6 (.D(signed__Imm5__1), .en(Clock), .Q(signed__Imm5__2), .clk(Clock));  // open: clr
  Register #(.width(16)) register_7 (
    .D(unsigned__Imm5__1), .en(Clock), .Q(unsigned__Imm5__2), .clk(Clock));  // open: clr
  Register #(.width(1)) register_8 (.D(MemWrite_1), .en(Clock), .Q(MemWrite_2), .clk(Clock));  // open: clr
  Register #(.width(1)) register_9 (.D(MemRead_1), .en(Clock), .Q(MemRead_2), .clk(Clock));  // open: clr
  Register #(.width(2)) register_10 (.D(ALUSrc_1), .en(Clock), .Q(ALUSrc_2), .clk(Clock));  // open: clr
  Register #(.width(1)) register_11 (.D(REG_write_1), .en(Clock), .Q(REG_write_2), .clk(Clock));  // open: clr
  Register #(.width(2)) register_12 (.D(MemtoReg_1), .en(Clock), .Q(MemtoReg_2), .clk(Clock));  // open: clr
  Register #(.width(4)) register_13 (.D(Alu_Signal_1), .en(Clock), .Q(Alu_Signal_2), .clk(Clock));  // open: clr
  Register #(.width(1)) register_14 (.D(LUI_0), .en(Clock), .Q(LUI_1), .clk(Clock));  // open: clr
endmodule
