// Logisim project IF-ID.circ as structural Verilog: 1 circuit, main circuit main
module main (
  input  [15:0] PC_1_0,
  input  [15:0] Instruction,
  input  [15:0] PC0,
  input  Stall,
  input  Clock,
  output [15:0] PC_1_1,
  output [15:0] Instruction_2,
  output [15:0] PC1
);

  wire not_1_out;

  not not_1 (not_1_out, Stall);
  Register #(.width(16)) register_1 (.D(PC_1_0), .en(not_1_out), .Q(PC_1_1), .clk(Clock));  // open: clr
  Register #(.width(16)) register_2 (.D(Instruction), .en(not_1_out), .Q(Instruction_2), .clk(Clock));  // open: clr
  Register #(.width(16)) register_3 (.D(PC0), .en(not_1_out), .Q(PC1), .clk(Clock));  // open: clr
endmodule
