// Logisim project MEM-WB.circ as structural Verilog: 1 circuit, main circuit main
module main (
  input  [15:0] PC_1_3,
  input  [15:0] BUSW_3,
  input  [2:0] RW_3,
  input  REG_write_3,
  input  CLOCK,
  output [15:0] PC_1_4,
  output [15:0] BUSW_4,
  output [2:0] RW_4,
  output REG_write_4
);

  Register #(.width(16)) register_1 (.D(PC_1_3), .en(CLOCK), .Q(PC_1_4), .clk(CLOCK));  // open: clr
  Register #(.width(16)) register_2 (.D(BUSW_3), .en(CLOCK), .Q(BUSW_4), .clk(CLOCK));  // open: clr
  Register #(.width(3)) register_3 (.D(RW_3), .en(CLOCK), .Q(RW_4), .clk(CLOCK));  // open: clr
  Register #(.width(1)) register_4 (.D(REG_write_3), .en(CLOCK), .Q(REG_write_4), .clk(CLOCK));  // open: clr
endmodule
