// Logisim project The main design.circ as structural Verilog: 11 circuits, main circuit main
// RegDst
module main (
  output out_1,
  output out_2
);

  wire Branch_Selc, Branch_Selc_1, Branch_Taken, Clock, Flush, ForwardC, ForwardD, I_type_Enable,
       I_type_Enable_1, J, JAL, JR, LUI, LUI1, MemRead, MemRead_1, MemRead_2, MemRead_3, MemWrite,
       MemWrite_1, MemWrite_2, MemWrite_3, not_1_out, or_2_out, R_type_Enable, R_type_Enable_1, REG_write,
       REG_write_1, REG_write_2, REG_write_3, REG_write_4, Stall;
  wire [1:0] ALUSrc, ALUSrc_1, ALUSrc_2, Func_1, Jump_Selc, Jump_Selc_1, MemtoReg, MemtoReg_1, MemtoReg_2,
       MemtoReg_3, RegDst, RegDst_1;
  wire [2:0] ForwardA, ForwardB, RW_1, RW_2, RW_3, RW_4;
  wire [3:0] Alu_Signal_1, Alu_Signal_2;
  wire [15:0] adder_2_out, adder_3_out, B, BUSA_1, BUSB_1, BUSW_3, BUSW_4, Instruction_0, Instruction_1,
       LUI_result_2, LUI_result_3, multiplexer_2_out, multiplexer_5_out, multiplexer_6_out,
       multiplexer_7_out, O_P_of_RAM_3, PC0, PC1, PC_1_0, PC_1_1, PC_1_2, PC_1_3, PC_1_4, Read_data_a_1,
       Read_data_a_2, Read_data_a_3, Read_data_b_1, Read_data_b_2, Read_data_b_3, register_file_1_out_9,
       register_file_1_out_10, register_file_1_out_11, register_file_1_out_12, register_file_1_out_13,
       register_file_1_out_14, register_file_1_out_15, register_file_1_out_16, Result_of_ALU_2,
       Result_of_ALU_3, rom_1_data, signed__Imm5__1, signed__Imm5__2, signed__Imm11__1, signed__Imm11__2,
       unsigned__Imm5__1, unsigned__Imm5__2;

  not not_1 (not_1_out, Stall);
  Clock clock_1 (.out(Clock));
  Register #(.width(16)) PC (.D(multiplexer_5_out), .en(not_1_out), .Q(PC0), .clk(Clock));  // open: clr
  Adder #(.width(16)) adder_1 (.a(16'h1), .b(PC0), .out(PC_1_0));  // open: cin, cout
  ROM #(.addrWidth(16), .dataWidth(16)) rom_1 (.addr(PC0), .data(rom_1_data));  // open: sel
  Control_Unit control_unit_1 (
    .REG_write(REG_write), .Jump_Selc(Jump_Selc), .ALUSrc(ALUSrc), .Branch_Selc(Branch_Selc),
    .MemtoReg(MemtoReg), .MemWrite(MemWrite), .MemRead(MemRead), .RegDst(RegDst),
    .OP_Code(Instruction_1[15:11]), .R_type_Enable(R_type_Enable), .I_type_Enable(I_type_Enable),
    .Branch_taken(Branch_Taken), .Func(Func_1), .JR(JR), .J(J), .JAL(JAL), .LUI(LUI));
  Multiplexer #(.width(16), .enable("false")) multiplexer_1 (
    .in0(rom_1_data), .in1({16{1'b0}}), .out(Instruction_0), .sel(Flush));
  Adder #(.width(16)) adder_2 (.a(PC1), .b(signed__Imm5__1), .out(adder_2_out));  // open: cin, cout
  IF_ID if_id_1 (
    .PC_1_0(PC_1_0), .Instruction(Instruction_0), .Stall(Stall), .Clock(Clock), .PC_1_1(PC_1_1),
    .Instruction_2({Instruction_1[15:11], Func_1, Instruction_1[8:0]}), .PC0(PC0), .PC1(PC1));
  Multiplexer #(.width(16), .enable("false")) multiplexer_2 (
    .in0(PC_1_0), .in1(adder_2_out), .out(multiplexer_2_out), .sel(Branch_Selc_1));
  Adder #(.width(16)) adder_3 (.a(PC1), .b(signed__Imm11__1), .out(adder_3_out));  // open: cin, cout
  Multiplexer #(.width(14), .enable("false")) multiplexer_3 (
    .in0({I_type_Enable, R_type_Enable, RegDst, MemtoReg, Branch_Selc, ALUSrc, Jump_Selc, REG_write, MemRead, MemWrite}),
    .in1({14{1'b0}}),
    .out({I_type_Enable_1, R_type_Enable_1, RegDst_1, MemtoReg_1, Branch_Selc_1, ALUSrc_1, Jump_Selc_1, REG_write_1, MemRead_1, MemWrite_1}),
    .sel(Stall));
  assign signed__Imm11__1 = {{5{Func_1[1]}}, {Func_1, Instruction_1[8:0]}};  // Bit_Extender bit_extender_1
  assign signed__Imm5__1 = {{11{Func_1[1]}}, {Func_1, Instruction_1[8:6]}};  // Bit_Extender bit_extender_2
  assign unsigned__Imm5__1 = {{11{1'b0}}, {Func_1, Instruction_1[8:6]}};  // Bit_Extender bit_extender_3
  Multiplexer #(.select(2), .width(3), .enable("false")) multiplexer_4 (
    .in0(Instruction_1[2:0]), .in1(Instruction_1[8:6]), .in2(3'b001), .in3(3'b111), .out(RW_1), .sel(RegDst_1));
  Multiplexer #(.select(2), .width(16), .enable("false")) multiplexer_5 (
    .in0(multiplexer_2_out), .in1(adder_3_out), .in2(Read_data_a_1), .out(multiplexer_5_out),
    .sel(Jump_Selc_1));  // open: in3
  // Probe on register_file_1_out_9
  // Probe on register_file_1_out_11
  // Probe on register_file_1_out_10
  // Probe on register_file_1_out_12
  // Probe on register_file_1_out_13
  Register_file register_file_1 (
    .RW(RW_4), .REG_write(REG_write_4), .BUS_W(BUSW_4), .Clock(Clock), .BUS_A(BUSA_1),
    .RS(Instruction_1[5:3]), .BUS_B(BUSB_1), .RT(Instruction_1[2:0]), .out_16(register_file_1_out_16),
    .out_15(register_file_1_out_15), .out_14(register_file_1_out_14), .out_13(register_file_1_out_13),
    .out_12(register_file_1_out_12), .out_11(register_file_1_out_11), .out_10(register_file_1_out_10),
    .out_9(register_file_1_out_9));
  // Probe on register_file_1_out_14
  // Probe on register_file_1_out_15
  // Probe on register_file_1_out_16
  or or_1 (Flush, JR, J, JAL, Branch_Taken);
  Multiplexer #(.width(16), .enable("false")) multiplexer_6 (
    .in0(Read_data_a_1), .in1(Result_of_ALU_3), .out(multiplexer_6_out), .sel(ForwardC));
  Comparator comparator_1 (
    .OP_code_1(Instruction_1[15:11]), .Read_data_a_1(multiplexer_6_out), .Read_data_b_1(multiplexer_7_out),
    .Taken(Branch_Taken));
  ALU_CONTROL alu_control_1 (
    .Selector_R_type({Instruction_1[11], Func_1}), .Enable1(R_type_Enable_1),
    .Selector_I_type(Instruction_1[15:11]), .Enable2(I_type_Enable_1), .ALU_signal(Alu_Signal_1));
  Multiplexer #(.width(16), .enable("false")) multiplexer_7 (
    .in0(Read_data_b_1), .in1(Result_of_ALU_3), .out(multiplexer_7_out), .sel(ForwardD));
  Multiplexer #(.select(3), .width(16), .enable("false")) multiplexer_8 (
    .in0(BUSA_1), .in1(BUSW_4), .in2(BUSW_3), .in3(Result_of_ALU_2), .in4(LUI_result_2), .out(Read_data_a_1),
    .sel(ForwardA));  // open: in5, in6, in7
  Multiplexer #(.select(3), .width(16), .enable("false")) multiplexer_9 (
    .in0(BUSB_1), .in1(BUSW_4), .in2(BUSW_3), .in3(Result_of_ALU_2), .in4(LUI_result_2), .out(Read_data_b_1),
    .sel(ForwardB));  // open: in5, in6, in7
  Hazard_Detect_Forward_and_Stall hazard_detect_forward_and_stall_1 (
    .RW_2(RW_2), .REG_write_2(REG_write_2), .Rs(Instruction_1[5:3]), .RW_3(RW_3), .REG_write_3(REG_write_3),
    .Rt(Instruction_1[2:0]), .MemRead_2(MemRead_2), .ForwardA(ForwardA), .Stall(Stall), .ForwardC(ForwardC),
    .ForwardD(ForwardD), .OP_code_1(Instruction_1[15:11]), .LUI(LUI1), .REG_write_4(REG_write_4),
    .RW_4(RW_4), .ForwardB(ForwardB));
  ID_EX id_ex_1 (
    .PC_1_1(PC_1_1), .BUSA_1(Read_data_a_1), .BUSB_1(Read_data_b_1), .RW_1(RW_1),
    .signed__Imm5__1(signed__Imm5__1), .unsigned__Imm5__1(unsigned__Imm5__1), .MemWrite_1(MemWrite_1),
    .MemRead_1(MemRead_1), .ALUSrc_1(ALUSrc_1), .REG_write_1(REG_write_1), .MemtoReg_1(MemtoReg_1),
    .Clock(Clock), .PC_1_2(PC_1_2), .BUSA_2(Read_data_a_2), .BUSB_2(Read_data_b_2), .RW_2(RW_2),
    .signed__Imm5__2(signed__Imm5__2), .unsigned__Imm5__2(unsigned__Imm5__2), .MemWrite_2(MemWrite_2),
    .MemRead_2(MemRead_2), .ALUSrc_2(ALUSrc_2), .REG_write_2(REG_write_2), .MemtoReg_2(MemtoReg_2),
    .Alu_Signal_1(Alu_Signal_1), .Alu_Signal_2(Alu_Signal_2), .signed__Imm11__1(signed__Imm11__1),
    .signed__Imm11__1_2(signed__Imm11__2), .LUI_0(LUI), .LUI_1(LUI1));
  Multiplexer #(.select(2), .width(16), .enable("false")) multiplexer_10 (
    .in0(Read_data_b_2), .in1(signed__Imm5__2), .in2(unsigned__Imm5__2), .out(B), .sel(ALUSrc_2));  // open: in3
  ALU alu_1 (
    .B(B), .A(Read_data_a_2), .ALU_signal(Alu_Signal_2), .ZERO_flag(out_1), .RESULT(Result_of_ALU_2),
    .Over_flow(out_2));
  Shifter #(.width(16)) shifter_1 (.in(signed__Imm11__2), .\dist (4'b0101), .out(LUI_result_2));
  EX_MEM ex_mem_1 (
    .PC_1_2(PC_1_2), .Result_of_ALU_2(Result_of_ALU_2), .RW_2(RW_2), .LUI_result_2(LUI_result_2),
    .BUSB_2(Read_data_b_2), .BUSA_2(Read_data_a_2), .MemWrite_2(MemWrite_2), .MemRead_2(MemRead_2),
    .REG_write_2(REG_write_2), .MemtoReg_2(MemtoReg_2), .CLOCK(Clock), .PC_1_3(PC_1_3),
    .Result_of_ALU_3(Result_of_ALU_3), .RW_3(RW_3), .LUI_result_3(LUI_result_3), .BUSB_3(Read_data_b_3),
    .BUSA_3(Read_data_a_3), .MemWrite_3(MemWrite_3), .MemRead_3(MemRead_3), .REG_write_3(REG_write_3),
    .MemtoReg_3(MemtoReg_3));
  or or_2 (or_2_out, MemWrite_3, MemRead_3);
  RAM #(.addrWidth(16), .dataWidth(16), .bus("separate")) ram_1 (
    .addr(Result_of_ALU_3), .din(Read_data_b_3), .data(O_P_of_RAM_3), .str(MemWrite_3), .sel(or_2_out),
    .clk(Clock), .ld(MemRead_3));  // open: clr
  Multiplexer #(.select(2), .width(16), .enable("false")) multiplexer_11 (
    .in0(Result_of_ALU_3), .in1(O_P_of_RAM_3), .in2(PC_1_3), .in3(LUI_result_3), .out(BUSW_3),
    .sel(MemtoReg_3));
  MEM_WB mem_wb_1 (
    .PC_1_3(PC_1_3), .BUSW_3(BUSW_3), .RW_3(RW_3), .REG_write_3(REG_write_3), .CLOCK(Clock), .PC_1_4(PC_1_4),
    .BUSW_4(BUSW_4), .RW_4(RW_4), .REG_write_4(REG_write_4));

  // Other names for the same wires on the sheet: Instruction_1[10:9] = Func_1; OP_code_1[4:0] = Instruction_1[15:11];
  //   Rt[2:0] = Instruction_1[2:0]; Rs[2:0] = Instruction_1[5:3]; Rd[2:0] = Instruction_1[8:6]; Over_Flow = out_2;
  //   ZERO_Flag = out_1

  // Notes on the sheet:
  //   contents of rom_1 (hex, n*v repeats v):
  //   9384 3b4d 4cd 6001 6042 6083 3aa4 b24 914 d93 70f0 88a 7700 6804 f804 4193 58de 7000 353 6001 614a
  //   618b 113 6804 1038
  //   Circuit of Control Unit And Alu_Signal
  //   Branches
  //   Circuit of PC
  //   for J and JAL
  //   for JR
  //   IMM10 0:10
  //   IMM5 6:10
  //   IMM5 6:10
  //   3:5 Rs
  //   0:2 Rt
  //   6:8 Rd
  //   OP code 11:15
  //   Func 9&10
  //   Content of registers
  //   Flush circuit
  //   FT and first bit
  //   of OP code
  //   Mark Amgad
  //   BY :  Abanob Evram
  //   Mina Moawad
  //   Department of electronics and communication
  //   Circuit of LUI
  //   for JAL
endmodule

module ALU (
  input  [15:0] B,
  input  [15:0] A,
  input  [3:0] ALU_signal,
  output ZERO_flag,
  output [15:0] RESULT,
  output Over_flow
);

  wire adder_1_cout, comparator_1_lt, comparator_2_lt, subtractor_1_bout, xor_2_out, xor_3_out;
  wire [15:0] adder_1_out, and_1_out, bit_extender_1_out, bit_extender_2_out, not_1_out, or_1_out,
       shifter_1_out, shifter_2_out, shifter_3_out, shifter_4_out, subtractor_1_out, xor_1_out;

  Comparator_part #(.width(16), .mode("unsigned")) comparator_1 (.a(A), .b(B), .lt(comparator_1_lt));  // open: gt, eq
  Comparator_part #(.width(16)) comparator_2 (.a(A), .b(B), .lt(comparator_2_lt));  // open: gt, eq
  assign and_1_out = A & B;  // AND_Gate and_1, 16 bits wide
  assign or_1_out = A | B;  // OR_Gate or_1, 16 bits wide
  assign xor_1_out = A ^ B;  // XOR_Gate xor_1, 16 bits wide
  Adder #(.width(16)) adder_1 (.a(A), .b(B), .out(adder_1_out), .cout(adder_1_cout));  // open: cin
  Subtractor #(.width(16)) subtractor_1 (.a(A), .b(B), .out(subtractor_1_out), .bout(subtractor_1_bout));  // open: bin
  assign not_1_out = ~or_1_out;  // NOT_Gate not_1, 16 bits wide
  Comparator_part #(.width(16)) comparator_3 (.a(A), .b(B), .eq(ZERO_flag));  // open: gt, lt
  Shifter #(.width(16)) shifter_1 (.in(A), .\dist (B[3:0]), .out(shifter_1_out));
  Shifter #(.width(16), .shift("lr")) shifter_2 (.in(A), .\dist (B[3:0]), .out(shifter_2_out));
  Shifter #(.width(16), .shift("ar")) shifter_3 (.in(A), .\dist (B[3:0]), .out(shifter_3_out));
  Shifter #(.width(16), .shift("rr")) shifter_4 (.in(A), .\dist (B[3:0]), .out(shifter_4_out));
  xor xor_2 (xor_2_out, adder_1_out[15], adder_1_cout);
  xor xor_3 (xor_3_out, subtractor_1_out[15], subtractor_1_bout);
  or or_2 (Over_flow, xor_2_out, xor_3_out);
  assign bit_extender_1_out = {{15{1'b0}}, comparator_2_lt};  // Bit_Extender bit_extender_1
  assign bit_extender_2_out = {{15{1'b0}}, comparator_1_lt};  // Bit_Extender bit_extender_2
  Multiplexer #(.select(4), .width(16), .enable("false")) multiplexer_1 (
    .in0(shifter_1_out), .in1(shifter_2_out), .in2(shifter_3_out), .in3(shifter_4_out), .in4(and_1_out),
    .in5(not_1_out), .in6(or_1_out), .in7(xor_1_out), .in8(adder_1_out), .in9(subtractor_1_out),
    .in10(bit_extender_1_out), .in11(bit_extender_2_out), .out(RESULT), .sel(ALU_signal));  // open: in12, in13, in14, in15

  // Notes on the sheet:
  //   First comparator : for check SLTU
  //   Second comparator :for check SLT,BEQ,BLT,BGE
  //   Shift amont 0:4
  //   SLL 0
  //   SRL 1
  //   SRA 2
  //   ROR 3
  //   AND 4
  //   NOR 5
  //   OR 6
  //   XOR 7
  //   ADD 8
  //   SUB 9
  //   SLT 10
  //   SLTU11
endmodule

module Register_file (
  input  [2:0] RS,
  input  [2:0] RW,
  input  [2:0] RT,
  input  REG_write,
  input  [15:0] BUS_W,
  input  Clock,
  output [15:0] BUS_A,
  output [15:0] BUS_B,
  output [15:0] out_9,
  output [15:0] out_10,
  output [15:0] out_11,
  output [15:0] out_12,
  output [15:0] out_13,
  output [15:0] out_14,
  output [15:0] out_15,
  output [15:0] out_16
);

  wire and_1_out, and_2_out, and_3_out, and_4_out, and_5_out, and_6_out, and_7_out, decoder_1_out1,
       decoder_1_out2, decoder_1_out3, decoder_1_out4, decoder_1_out5, decoder_1_out6, decoder_1_out7;

  Decoder #(.select(3), .enable("false")) decoder_1 (
    .out1(decoder_1_out1), .out2(decoder_1_out2), .out3(decoder_1_out3), .out4(decoder_1_out4),
    .out5(decoder_1_out5), .out6(decoder_1_out6), .out7(decoder_1_out7), .sel(RW));  // open: out0
  and and_1 (and_1_out, decoder_1_out1, REG_write);
  and and_2 (and_2_out, decoder_1_out2, REG_write);
  and and_3 (and_3_out, decoder_1_out3, REG_write);
  and and_4 (and_4_out, decoder_1_out4, REG_write);
  and and_5 (and_5_out, decoder_1_out5, REG_write);
  and and_6 (and_6_out, decoder_1_out6, REG_write);
  and and_7 (and_7_out, decoder_1_out7, REG_write);
  Register #(.width(16)) R1 (.D(BUS_W), .en(and_1_out), .Q(out_15), .clk(Clock));  // open: clr
  Register #(.width(16)) R2 (.D(BUS_W), .en(and_2_out), .Q(out_14), .clk(Clock));  // open: clr
  Register #(.width(16)) R3 (.D(BUS_W), .en(and_3_out), .Q(out_13), .clk(Clock));  // open: clr
  Register #(.width(16)) R4 (.D(BUS_W), .en(and_4_out), .Q(out_12), .clk(Clock));  // open: clr
  Register #(.width(16)) R5 (.D(BUS_W), .en(and_5_out), .Q(out_11), .clk(Clock));  // open: clr
  Register #(.width(16)) R6 (.D(BUS_W), .en(and_6_out), .Q(out_10), .clk(Clock));  // open: clr
  Register #(.width(16)) R7 (.D(BUS_W), .en(and_7_out), .Q(out_9), .clk(Clock));  // open: clr
  Multiplexer #(.select(3), .width(16), .enable("false")) multiplexer_1 (
    .in0({16{1'b0}}), .in1(out_15), .in2(out_14), .in3(out_13), .in4(out_12), .in5(out_11), .in6(out_10),
    .in7(out_9), .out(BUS_A), .sel(RS));
  Multiplexer #(.select(3), .width(16), .enable("false")) multiplexer_2 (
    .in0({16{1'b0}}), .in1(out_15), .in2(out_14), .in3(out_13), .in4(out_12), .in5(out_11), .in6(out_10),
    .in7(out_9), .out(BUS_B), .sel(RT));

  assign out_16 = {16{1'b0}};

  // Other names for the same wires on the sheet: R1[15:0] = out_15; R2[15:0] = out_14; R3[15:0] = out_13;
  //   R4[15:0] = out_12; R5[15:0] = out_11; R6[15:0] = out_10; R7[15:0] = out_9

  // Notes on the sheet:
  //   R0
endmodule

// ALU_Signal
module ALU_CONTROL (
  input  [2:0] Selector_R_type,
  input  Enable1,
  input  [4:0] Selector_I_type,
  input  Enable2,
  output [3:0] ALU_signal
);

  wire [3:0] multiplexer_1_out, multiplexer_2_out;

  Multiplexer #(.select(3), .width(4)) multiplexer_1 (
    .in0(4'b0100), .in1(4'b0110), .in2(4'b0111), .in3(4'b0101), .in4(4'b1000), .in5(4'b1001), .in6(4'b1010),
    .in7(4'b1011), .out(multiplexer_1_out), .sel(Selector_R_type), .en(Enable1));
  Multiplexer #(.select(5), .width(4)) multiplexer_2 (
    .in4(4'b0100), .in5(4'b0110), .in6(4'b0111), .in7(4'b1000), .in8(4'b0000), .in9(4'b0001), .in10(4'b0010),
    .in11(4'b0011), .in12(4'b1000), .in13(4'b1000), .out(multiplexer_2_out), .sel(Selector_I_type),
    .en(Enable2));  // open: in0, in1, in2, in3, in14, in15, in16, in17, in18, in19, in20, in21, in22, in23, in24, in25, in26, in27, in28, in29, in30, in31
  Multiplexer #(.width(4), .enable("false")) multiplexer_3 (
    .in0(multiplexer_1_out), .in1(multiplexer_2_out), .out(ALU_signal), .sel(Enable2));

  // Notes on the sheet:
  //   First MUX
  //   Second MUX
  //   R_TYPE
  //   I_Type
  //   if the enable of the second mux is 0 then the second mux is disabled and the main mux selector is 0 which is the first mux output
  //   Main MUX
endmodule

module Control_Unit (
  input  Branch_taken,
  input  [1:0] Func,
  input  [4:0] OP_Code,
  output REG_write,
  output JR,
  output J,
  output JAL,
  output LUI,
  output [1:0] Jump_Selc,
  output [1:0] ALUSrc,
  output MemWrite,
  output MemRead,
  output Branch_Selc,
  output R_type_Enable,
  output [1:0] MemtoReg,
  output [1:0] RegDst,
  output I_type_Enable
);

  wire AddI, and_2_out, and_3_out, and_4_out, and_5_out, ANDI, BEQ, BGE, BLT, BNE, Branch_taken_t,
       decoder_1_out0, decoder_1_out1, not_1_out, not_2_out, ORI, priority_encoder_1_p2,
       priority_encoder_2_p2, priority_encoder_2_p3, priority_encoder_2_p4, priority_encoder_3_p2,
       priority_encoder_3_p3, priority_encoder_3_p4, priority_encoder_4_p2, ROR, SLL, SRA, SRL, XORI;

  Decoder #(.select(5), .enable("false")) decoder_1 (
    .out0(decoder_1_out0), .out1(decoder_1_out1), .out2(JR), .out4(ANDI), .out5(ORI), .out6(XORI),
    .out7(AddI), .out8(SLL), .out9(SRL), .out10(SRA), .out11(ROR), .out12(MemRead), .out13(MemWrite),
    .out14(BEQ), .out15(BNE), .out16(BLT), .out17(BGE), .out18(LUI), .out30(J), .out31(JAL), .sel(OP_Code));  // open: out3, out19, out20, out21, out22, out23, out24, out25, out26, out27, out28, out29
  or or_1 (I_type_Enable, MemRead, ANDI, ORI, XORI, AddI, SLL, SRL, SRA, ROR, BEQ, BNE, BLT, BGE, MemWrite);
  or or_2 (R_type_Enable, decoder_1_out0, decoder_1_out1);
  or or_3 (REG_write, SLL, R_type_Enable, ANDI, ORI, XORI, AddI, SRL, SRA, ROR, MemRead, JAL, LUI);
  // Priority_Encoder #(.select(2)) priority_encoder_1: pin names not known; wires that end beside it: RegDst, priority_encoder_1_p2, R_type_Enable, LUI, JAL
  // Priority_Encoder #(.select(2)) priority_encoder_2: pin names not known; wires that end beside it: ALUSrc, priority_encoder_2_p2, priority_encoder_2_p3, priority_encoder_2_p4
  or or_4 (priority_encoder_2_p4, ANDI, ORI, XORI, SLL, SRL, SRA, ROR);
  or or_5 (priority_encoder_1_p2, ANDI, ORI, XORI, AddI, SLL, SRL, SRA, ROR, MemRead);
  or or_6 (priority_encoder_2_p2, R_type_Enable, BEQ, BNE, BLT, BGE);
  or or_7 (priority_encoder_2_p3, AddI, MemRead, MemWrite);
  or or_8 (Branch_Selc, and_2_out, and_3_out, and_4_out, and_5_out);
  // Priority_Encoder #(.select(2)) priority_encoder_3: pin names not known; wires that end beside it: Jump_Selc, priority_encoder_3_p2, priority_encoder_3_p3, priority_encoder_3_p4
  // Priority_Encoder #(.select(2)) priority_encoder_4: pin names not known; wires that end beside it: MemtoReg, priority_encoder_4_p2, MemRead, JAL, LUI
  or or_9 (priority_encoder_3_p2, R_type_Enable, ANDI, ORI, XORI, AddI, SLL, SRL, SRA, ROR, MemRead, MemWrite, BEQ, BNE, BLT, BGE, LUI);
  or or_10 (priority_encoder_3_p3, J, JAL);
  and and_1 (priority_encoder_3_p4, JR, not_1_out, not_2_out);
  and and_2 (and_2_out, BEQ, Branch_taken_t);
  and and_3 (and_3_out, BNE, Branch_taken_t);
  and and_4 (and_4_out, BLT, Branch_taken_t);
  and and_5 (and_5_out, BGE, Branch_taken_t);
  or or_11 (priority_encoder_4_p2, R_type_Enable, ANDI, ORI, XORI, AddI, SLL, SRL, SRA, ROR);
  not not_1 (not_1_out, Func[0]);
  not not_2 (not_2_out, Func[1]);

  // Other names for the same wires on the sheet: LW = MemRead; R_Type = R_type_Enable; SW = MemWrite

  // Notes on the sheet:
  //   Enable for ALU Control Unit
  //   O/P for control hazard
  //   if 0 Rt is slected
  //      1 Rd is sleced
  //     2 R1 is slected
  //   3 R7 is slected
  //   allow to write
  //     1 signed (Imm5)
  //   if 1 REG write is Enable
  //   if 0 BUSB  is activated
  //   2 unsigned (Imm5)
  //   3 to LUI
  //   0 to  ALU Operations
  //   1 to select load 
  //   2 to select JAL
  //   0 for branches or PC+1
  //   1 for J and JAL
  //   2 for JR
endmodule

module IF_ID (
  input  [15:0] PC_1_0,
  input  [15:0] Instruction,
  input  [15:0] PC0,
  input  Stall,
  input  Clock,
  output [15:0] PC_1_1,
  output [15:0] Instruction_2,
  output [15:0] PC1
);

  wire not_1_out;

  not not_1 (not_1_out, Stall);
  Register #(.width(16)) register_1 (.D(PC_1_0), .en(not_1_out), .Q(PC_1_1), .clk(Clock));  // open: clr
  Register #(.width(16)) register_2 (.D(Instruction), .en(not_1_out), .Q(Instruction_2), .clk(Clock));  // open: clr
  Register #(.width(16)) register_3 (.D(PC0), .en(not_1_out), .Q(PC1), .clk(Clock));  // open: clr
endmodule

module ID_EX (
  input  [15:0] signed__Imm11__1,
  input  [15:0] PC_1_1,
  input  [15:0] BUSA_1,
  input  [15:0] BUSB_1,
  input  [2:0] RW_1,
  input  [15:0] signed__Imm5__1,
  input  [15:0] unsigned__Imm5__1,
  input  MemWrite_1,
  input  MemRead_1,
  input  [1:0] ALUSrc_1,
  input  REG_write_1,
  input  [1:0] MemtoReg_1,
  input  [3:0] Alu_Signal_1,
  input  LUI_0,
  input  Clock,
  output [15:0] signed__Imm11__1_2,
  output [15:0] PC_1_2,
  output [15:0] BUSA_2,
  output [15:0] BUSB_2,
  output [2:0] RW_2,
  output [15:0] signed__Imm5__2,
  output [15:0] unsigned__Imm5__2,
  output MemWrite_2,
  output MemRead_2,
  output [1:0] ALUSrc_2,
  output REG_write_2,
  output [1:0] MemtoReg_2,
  output [3:0] Alu_Signal_2,
  output LUI_1
);

  Register #(.width(16)) register_1 (
    .D(signed__Imm11__1), .en(Clock), .Q(signed__Imm11__1_2), .clk(Clock));  // open: clr
  Register #(.width(16)) register_2 (.D(PC_1_1), .en(Clock), .Q(PC_1_2), .clk(Clock));  // open: clr
  Register #(.width(16)) register_3 (.D(BUSA_1), .en(Clock), .Q(BUSA_2), .clk(Clock));  // open: clr
  Register #(.width(16)) register_4 (.D(BUSB_1), .en(Clock), .Q(BUSB_2), .clk(Clock));  // open: clr
  Register #(.width(3)) register_5 (.D(RW_1), .en(Clock), .Q(RW_2), .clk(Clock));  // open: clr
  Register #(.width(16)) register_6 (.D(signed__Imm5__1), .en(Clock), .Q(signed__Imm5__2), .clk(Clock));  // open: clr
  Register #(.width(16)) register_7 (
    .D(unsigned__Imm5__1), .en(Clock), .Q(unsigned__Imm5__2), .clk(Clock));  // open: clr
  Register #(.width(1)) register_8 (.D(MemWrite_1), .en(Clock), .Q(MemWrite_2), .clk(Clock));  // open: clr
  Register #(.width(1)) register_9 (.D(MemRead_1), .en(Clock), .Q(MemRead_2), .clk(Clock));  // open: clr
  Register #(.width(2)) register_10 (.D(ALUSrc_1), .en(Clock), .Q(ALUSrc_2), .clk(Clock));  // open: clr
  Register #(.width(1)) register_11 (.D(REG_write_1), .en(Clock), .Q(REG_write_2), .clk(Clock));  // open: clr
  Register #(.width(2)) register_12 (.D(MemtoReg_1), .en(Clock), .Q(MemtoReg_2), .clk(Clock));  // open: clr
  Register #(.width(4)) register_13 (.D(Alu_Signal_1), .en(Clock), .Q(Alu_Signal_2), .clk(Clock));  // open: clr
  Register #(.width(1)) register_14 (.D(LUI_0), .en(Clock), .Q(LUI_1), .clk(Clock));  // open: clr
endmodule

module EX_MEM (
  input  [15:0] PC_1_2,
  input  [15:0] Result_of_ALU_2,
  input  [2:0] RW_2,
  input  [15:0] LUI_result_2,
  input  [15:0] BUSB_2,
  input  [15:0] BUSA_2,
  input  MemWrite_2,
  input  MemRead_2,
  input  REG_write_2,
  input  [1:0] MemtoReg_2,
  input  CLOCK,
  output [15:0] PC_1_3,
  output [15:0] Result_of_ALU_3,
  output [2:0] RW_3,
  output [15:0] LUI_result_3,
  output [15:0] BUSB_3,
  output [15:0] BUSA_3,
  output MemWrite_3,
  output MemRead_3,
  output REG_write_3,
  output [1:0] MemtoReg_3
);

  Register #(.width(16)) register_1 (.D(PC_1_2), .en(CLOCK), .Q(PC_1_3), .clk(CLOCK));  // open: clr
  Register #(.width(16)) register_2 (.D(Result_of_ALU_2), .en(CLOCK), .Q(Result_of_ALU_3), .clk(CLOCK));  // open: clr
  Register #(.width(3)) register_3 (.D(RW_2), .en(CLOCK), .Q(RW_3), .clk(CLOCK));  // open: clr
  Register #(.width(16)) register_4 (.D(LUI_result_2), .en(CLOCK), .Q(LUI_result_3), .clk(CLOCK));  // open: clr
  Register #(.width(16)) register_5 (.D(BUSB_2), .en(CLOCK), .Q(BUSB_3), .clk(CLOCK));  // open: clr
  Register #(.width(16)) register_6 (.D(BUSA_2), .en(CLOCK), .Q(BUSA_3), .clk(CLOCK));  // open: clr
  Register #(.width(1)) register_7 (.D(MemWrite_2), .en(CLOCK), .Q(MemWrite_3), .clk(CLOCK));  // open: clr
  Register #(.width(1)) register_8 (.D(MemRead_2), .en(CLOCK), .Q(MemRead_3), .clk(CLOCK));  // open: clr
  Register #(.width(1)) register_9 (.D(REG_write_2), .en(CLOCK), .Q(REG_write_3), .clk(CLOCK));  // open: clr
  Register #(.width(2)) register_10 (.D(MemtoReg_2), .en(CLOCK), .Q(MemtoReg_3), .clk(CLOCK));  // open: clr
endmodule

module MEM_WB (
  input  [15:0] PC_1_3,
  input  [15:0] BUSW_3,
  input  [2:0] RW_3,
  input  REG_write_3,
  input  CLOCK,
  output [15:0] PC_1_4,
  output [15:0] BUSW_4,
  output [2:0] RW_4,
  output REG_write_4
);

  Register #(.width(16)) register_1 (.D(PC_1_3), .en(CLOCK), .Q(PC_1_4), .clk(CLOCK));  // open: clr
  Register #(.width(16)) register_2 (.D(BUSW_3), .en(CLOCK), .Q(BUSW_4), .clk(CLOCK));  // open: clr
  Register #(.width(3)) register_3 (.D(RW_3), .en(CLOCK), .Q(RW_4), .clk(CLOCK));  // open: clr
  Register #(.width(1)) register_4 (.D(REG_write_3), .en(CLOCK), .Q(REG_write_4), .clk(CLOCK));  // open: clr
endmodule

module Comparator (
  input  [4:0] OP_code_1,
  input  [15:0] Read_data_a_1,
  input  [15:0] Read_data_b_1,
  output Taken
);

  wire BEQ_out, BGE_out, BLT_out, BNE_out, comparator_1_eq, comparator_1_lt;

  Comparator_part #(.width(16)) comparator_1 (
    .a(Read_data_a_1), .b(Read_data_b_1), .eq(comparator_1_eq), .lt(comparator_1_lt));  // open: gt
  and BEQ (BEQ_out, ~OP_code_1[4], OP_code_1[3], OP_code_1[2], OP_code_1[1], ~OP_code_1[0], comparator_1_eq);  // AND_Gate
  and BNE (BNE_out, ~OP_code_1[4], OP_code_1[3], OP_code_1[2], OP_code_1[1], OP_code_1[0], ~comparator_1_eq);  // AND_Gate
  or or_1 (Taken, BEQ_out, BNE_out, BLT_out, BGE_out);
  and BLT (BLT_out, OP_code_1[4], ~OP_code_1[3], ~OP_code_1[2], ~OP_code_1[1], ~OP_code_1[0], comparator_1_lt);  // AND_Gate
  and BGE (BGE_out, OP_code_1[4], ~OP_code_1[3], ~OP_code_1[2], ~OP_code_1[1], OP_code_1[0], ~comparator_1_lt);  // AND_Gate

  // Other names for the same wires on the sheet: BIT0 = OP_code_1[0]; BIT1 = OP_code_1[1]; BIT2 = OP_code_1[2];
  //   BIT3 = OP_code_1[3]; BIT4 = OP_code_1[4]

  // Notes on the sheet:
  //   checks if a branch is taken or not
  //   is taken
  //   Op code is splitted into 5 bits to know which
endmodule

module Hazard_Detect_Forward_and_Stall (
  input  [2:0] RW_2,
  input  REG_write_2,
  input  [2:0] Rs,
  input  [2:0] RW_3,
  input  REG_write_3,
  input  [2:0] Rt,
  input  REG_write_4,
  input  LUI,
  input  [2:0] RW_4,
  input  MemRead_2,
  input  [4:0] OP_code_1,
  output Stall,
  output [2:0] ForwardB,
  output [2:0] ForwardA,
  output ForwardC,
  output ForwardD
);

  wire and_2_out, and_3_out, and_4_out, and_5_out, and_8_out, and_9_out, and_10_out, and_11_out, BEQ, BGE,
       BLT, BNE, comparator_1_eq, comparator_2_eq, comparator_3_eq, comparator_4_eq, comparator_5_eq,
       comparator_6_eq, comparator_7_eq, comparator_8_eq, comparator_9_eq, comparator_10_eq,
       comparator_11_eq, comparator_12_eq, comparator_13_eq, comparator_14_eq, comparator_15_eq,
       comparator_16_eq, comparator_17_eq, comparator_18_eq, comparator_19_eq, comparator_20_eq,
       comparator_21_eq, comparator_22_eq, nor_1_out, nor_2_out, or_1_out, or_2_out, or_3_out;

  or or_1 (or_1_out, BEQ, BNE, BLT, BGE);
  Comparator_part #(.width(3), .mode("unsigned")) comparator_1 (
    .a(RW_3), .b(3'b000), .eq(comparator_1_eq));  // open: gt, lt
  Comparator_part #(.width(3), .mode("unsigned")) comparator_2 (
    .a(RW_3), .b(Rs), .eq(comparator_2_eq));  // open: gt, lt
  Comparator_part #(.width(3), .mode("unsigned")) comparator_3 (
    .a(Rs), .b(3'b000), .eq(comparator_3_eq));  // open: gt, lt
  Comparator_part #(.width(3), .mode("unsigned")) comparator_4 (
    .a(Rs), .b(RW_4), .eq(comparator_4_eq));  // open: gt, lt
  Comparator_part #(.width(3), .mode("unsigned")) comparator_5 (
    .a(Rs), .b(3'b000), .eq(comparator_5_eq));  // open: gt, lt
  Comparator_part #(.width(3), .mode("unsigned")) comparator_6 (
    .a(Rs), .b(RW_3), .eq(comparator_6_eq));  // open: gt, lt
  Comparator_part #(.width(3), .mode("unsigned")) comparator_7 (
    .a(Rs), .b(3'b000), .eq(comparator_7_eq));  // open: gt, lt
  Comparator_part #(.width(3), .mode("unsigned")) comparator_8 (
    .a(Rs), .b(RW_2), .eq(comparator_8_eq));  // open: gt, lt
  Comparator_part #(.width(3), .mode("unsigned")) comparator_9 (
    .a(Rs), .b(3'b000), .eq(comparator_9_eq));  // open: gt, lt
  Comparator_part #(.width(3), .mode("unsigned")) comparator_10 (
    .a(Rs), .b(RW_2), .eq(comparator_10_eq));  // open: gt, lt
  and and_1 (ForwardC, or_1_out, ~comparator_1_eq, comparator_2_eq);  // AND_Gate
  and and_2 (and_2_out, ~comparator_3_eq, comparator_4_eq, REG_write_4);  // AND_Gate
  and and_3 (and_3_out, ~comparator_5_eq, comparator_6_eq, REG_write_3);  // AND_Gate
  and and_4 (and_4_out, ~comparator_7_eq, comparator_8_eq, REG_write_2);  // AND_Gate
  and and_5 (and_5_out, ~comparator_9_eq, comparator_10_eq, REG_write_2, LUI);  // AND_Gate
  Comparator_part #(.width(3), .mode("unsigned")) comparator_11 (
    .a(ForwardA), .b(3'b011), .eq(comparator_11_eq));  // open: gt, lt
  Comparator_part #(.width(3), .mode("unsigned")) comparator_12 (
    .a(3'b011), .b(ForwardB), .eq(comparator_12_eq));  // open: gt, lt
  nor nor_1 (nor_1_out, and_2_out, and_3_out, and_4_out, and_5_out);
  Priority_Encoder priority_encoder_1 (
    .in0(nor_1_out), .in1(and_2_out), .in2(and_3_out), .in3(and_4_out), .in4(and_5_out), .out(ForwardA));  // open: in5, in6, in7, en_in, gs, en_out
  Comparator_part #(.width(3), .mode("unsigned")) comparator_13 (
    .a(RW_3), .b(3'b000), .eq(comparator_13_eq));  // open: gt, lt
  Comparator_part #(.width(3), .mode("unsigned")) comparator_14 (
    .a(RW_3), .b(Rt), .eq(comparator_14_eq));  // open: gt, lt
  or or_2 (or_2_out, comparator_11_eq, comparator_12_eq);
  or or_3 (or_3_out, BEQ, BNE, BLT, BGE);
  and and_6 (Stall, or_2_out, MemRead_2);
  and and_7 (ForwardD, or_3_out, ~comparator_13_eq, comparator_14_eq);  // AND_Gate
  Comparator_part #(.width(3), .mode("unsigned")) comparator_15 (
    .a(Rt), .b(3'b000), .eq(comparator_15_eq));  // open: gt, lt
  Comparator_part #(.width(3), .mode("unsigned")) comparator_16 (
    .a(Rt), .b(RW_4), .eq(comparator_16_eq));  // open: gt, lt
  Comparator_part #(.width(3), .mode("unsigned")) comparator_17 (
    .a(Rt), .b(3'b000), .eq(comparator_17_eq));  // open: gt, lt
  Comparator_part #(.width(3), .mode("unsigned")) comparator_18 (
    .a(Rt), .b(RW_3), .eq(comparator_18_eq));  // open: gt, lt
  Comparator_part #(.width(3), .mode("unsigned")) comparator_19 (
    .a(Rt), .b(3'b000), .eq(comparator_19_eq));  // open: gt, lt
  Comparator_part #(.width(3), .mode("unsigned")) comparator_20 (
    .a(Rt), .b(RW_2), .eq(comparator_20_eq));  // open: gt, lt
  Comparator_part #(.width(3), .mode("unsigned")) comparator_21 (
    .a(Rt), .b(3'b000), .eq(comparator_21_eq));  // open: gt, lt
  Comparator_part #(.width(3), .mode("unsigned")) comparator_22 (
    .a(Rt), .b(RW_2), .eq(comparator_22_eq));  // open: gt, lt
  and and_8 (and_8_out, ~comparator_15_eq, comparator_16_eq, REG_write_4);  // AND_Gate
  and and_9 (and_9_out, ~comparator_17_eq, comparator_18_eq, REG_write_3);  // AND_Gate
  and and_10 (and_10_out, ~comparator_19_eq, comparator_20_eq, REG_write_2);  // AND_Gate
  and and_11 (and_11_out, ~comparator_21_eq, comparator_22_eq, REG_write_2, LUI);  // AND_Gate
  Decoder #(.select(5), .enable("false")) decoder_1 (
    .out14(BEQ), .out15(BNE), .out16(BLT), .out17(BGE), .sel(OP_code_1));  // open: out0, out1, out2, out3, out4, out5, out6, out7, out8, out9, out10, out11, out12, out13, out18, out19, out20, out21, out22, out23, out24, out25, out26, out27, out28, out29, out30, out31
  nor nor_2 (nor_2_out, and_8_out, and_9_out, and_10_out, and_11_out);
  Priority_Encoder priority_encoder_2 (
    .in0(nor_2_out), .in1(and_8_out), .in2(and_9_out), .in3(and_10_out), .in4(and_11_out), .out(ForwardB));  // open: in5, in6, in7, en_in, gs, en_out

  // Notes on the sheet:
  //   encoder to generate the signal of forwardA mux 
  //   priority is taken into consideration
  //   MEM/WB
  //   EX/MEM
  //   ALU
  //   Result of Lui
  //   forwardC and forwardD are muxs used in the comparator 
  //   to detect branches
  //   if A=1, B=1
  //   implementaion circuit of stall.
  //   and EX.memread =1 + LUI = 1
  //   MEM/WB
  //   EX/MEM
  //   ALU
  //   Result of Lui
  //   encoder to generate the signal of forwardB mux 
  //   priority is taken into consideration
endmodule
