// Logisim project ALU CONTROL.circ as structural Verilog: 1 circuit, main circuit ALU CONTROL
module ALU_CONTROL (
  input  [2:0] Selector_R_type,
  input  Enable1,
  input  [4:0] Selector_I_type,
  input  Enable2,
  output [3:0] ALU_signal
);

  wire [3:0] multiplexer_1_out, multiplexer_2_out;

  Multiplexer #(.select(3), .width(4)) multiplexer_1 (
    .in0(4'b0100), .in1(4'b0110), .in2(4'b0111), .in3(4'b0101), .in4(4'b1000), .in5(4'b1001), .in6(4'b1010),
    .in7(4'b1011), .out(multiplexer_1_out), .sel(Selector_R_type), .en(Enable1));
  Multiplexer #(.select(5), .width(4)) multiplexer_2 (
    .in4(4'b0100), .in5(4'b0110), .in6(4'b0111), .in7(4'b1000), .in8(4'b0000), .in9(4'b0001), .in10(4'b0010),
    .in11(4'b0011), .in12(4'b1000), .in13(4'b1000), .in14(4'b1100), .in15(4'b1101), .in16(4'b1110),
    .in17(4'b1111), .out(multiplexer_2_out), .sel(Selector_I_type), .en(Enable2));  // open: in0, in1, in2, in3, in18, in19, in20, in21, in22, in23, in24, in25, in26, in27, in28, in29, in30, in31
  Multiplexer #(.width(4), .enable("false")) multiplexer_3 (
    .in0(multiplexer_1_out), .in1(multiplexer_2_out), .out(ALU_signal), .sel(Enable2));

  // Notes on the sheet:
  //   First MUX
  //   Second MUX
  //   R_TYPE
  //   I_Type
  //   if the enable of the second mux is 0 then the second mux is disabled and the main mux selector is 0 which is the first mux output
  //   Main MUX
endmodule
