// Logisim project Control Unit.circ as structural Verilog: 1 circuit, main circuit Control Unit
module Control_Unit (
  input  Zero_Flag,
  input  Result_of_ALU,
  input  [1:0] Func,
  input  [4:0] OP_Code,
  output REG_write,
  output [1:0] Jump_Selc,
  output [1:0] ALUSrc,
  output MemWrite,
  output MemRead,
  output Branch_Selc,
  output MEM_Enable,
  output R_type_Enable,
  output [1:0] MemtoReg,
  output [1:0] RegDst,
  output I_type_Enable
);

  wire AddI, and_2_out, and_3_out, and_4_out, and_5_out, ANDI, BEQ, BGE, BLT, BNE, decoder_1_out0,
       decoder_1_out1, J, JAL, JR, LUI, not_1_out, not_2_out, not_3_out, ORI, priority_encoder_1_p2,
       priority_encoder_2_p2, priority_encoder_2_p3, priority_encoder_2_p4, priority_encoder_3_p2,
       priority_encoder_3_p3, priority_encoder_3_p4, priority_encoder_4_p2, ROR, SLL, SRA, SRL, XORI;

  Decoder #(.select(5), .enable("false")) decoder_1 (
    .out0(decoder_1_out0), .out1(decoder_1_out1), .out2(JR), .out4(ANDI), .out5(ORI), .out6(XORI),
    .out7(AddI), .out8(SLL), .out9(SRL), .out10(SRA), .out11(ROR), .out12(MemRead), .out13(MemWrite),
    .out14(BEQ), .out15(BNE), .out16(BLT), .out17(BGE), .out18(LUI), .out30(J), .out31(JAL), .sel(OP_Code));  // open: out3, out19, out20, out21, out22, out23, out24, out25, out26, out27, out28, out29
  or or_1 (MEM_Enable, MemWrite, MemRead);
  or or_2 (I_type_Enable, MemRead, ANDI, ORI, XORI, AddI, SLL, SRL, SRA, ROR, BEQ, BNE, BLT, BGE, MemWrite);
  or or_3 (R_type_Enable, decoder_1_out0, decoder_1_out1);
  or or_4 (REG_write, SLL, R_type_Enable, ANDI, ORI, XORI, AddI, SRL, SRA, ROR, MemRead, JAL, LUI);
  // Priority_Encoder #(.select(2)) priority_encoder_1: pin names not known; wires that end beside it: RegDst, priority_encoder_1_p2, R_type_Enable, LUI, JAL
  // Priority_Encoder #(.select(2)) priority_encoder_2: pin names not known; wires that end beside it: ALUSrc, priority_encoder_2_p2, priority_encoder_2_p3, priority_encoder_2_p4
  or or_5 (priority_encoder_2_p4, ANDI, ORI, XORI, SLL, SRL, SRA, ROR);
  or or_6 (priority_encoder_1_p2, ANDI, ORI, XORI, AddI, SLL, SRL, SRA, ROR, MemRead);
  or or_7 (priority_encoder_2_p2, R_type_Enable, BEQ, BNE, BLT, BGE);
  or or_8 (priority_encoder_2_p3, AddI, MemRead, MemWrite);
  or or_9 (Branch_Selc, and_2_out, and_3_out, and_4_out, and_5_out);
  // Priority_Encoder #(.select(2)) priority_encoder_3: pin names not known; wires that end beside it: Jump_Selc, priority_encoder_3_p2, priority_encoder_3_p3, priority_encoder_3_p4
  // Priority_Encoder #(.select(2)) priority_encoder_4: pin names not known; wires that end beside it: MemtoReg, priority_encoder_4_p2, MemRead, JAL, LUI
  or or_10 (priority_encoder_3_p2, R_type_Enable, ANDI, ORI, XORI, AddI, SLL, SRL, SRA, ROR, MemRead, MemWrite, BEQ, BNE, BLT, BGE, LUI);
  or or_11 (priority_encoder_3_p3, J, JAL);
  and and_1 (priority_encoder_3_p4, JR, not_1_out, not_2_out);
  and and_2 (and_2_out, BEQ, Zero_Flag);
  and and_3 (and_3_out, BNE, not_3_out);
  and and_4 (and_4_out, BLT, Result_of_ALU);
  and and_5 (and_5_out, BGE, Result_of_ALU);
  or or_12 (priority_encoder_4_p2, R_type_Enable, ANDI, ORI, XORI, AddI, SLL, SRL, SRA, ROR);
  not not_1 (not_1_out, Func[0]);
  not not_2 (not_2_out, Func[1]);
  not not_3 (not_3_out, Zero_Flag);

  // Other names for the same wires on the sheet: LW = MemRead; R_Type = R_type_Enable; SW = MemWrite

  // Notes on the sheet:
  //   Enable for ALU Control Unit
  //   if 0 Rt is slected
  //      1 Rd is sleced
  //     2 R1 is slected
  //   3 R7 is slected
  //   allow to write
  //     1 signed (Imm5)
  //   if 1 REG write is Enable
  //   if 0 BUSB  is activated
  //   2 unsigned (Imm5)
  //   0 to  ALU Operations
  //   1 to select load 
  //   2 to select PC+1
  //   3 to result of (LUI)
  //   0 for branches or PC+1
  //   1 for J and JAL
  //   2 for JR
endmodule
