// Logisim project Register file.circ as structural Verilog: 1 circuit, main circuit Register file
module Register_file (
  input  [2:0] RS,
  input  [2:0] RW,
  input  [2:0] RT,
  input  REG_write,
  input  [15:0] BUS_W,
  input  Clock,
  output [15:0] BUS_A,
  output [15:0] BUS_B,
  output [15:0] out_9,
  output [15:0] out_10,
  output [15:0] out_11,
  output [15:0] out_12,
  output [15:0] out_13,
  output [15:0] out_14,
  output [15:0] out_15,
  output [15:0] out_16
);

  wire and_1_out, and_2_out, and_3_out, and_4_out, and_5_out, and_6_out, and_7_out, decoder_1_out1,
       decoder_1_out2, decoder_1_out3, decoder_1_out4, decoder_1_out5, decoder_1_out6, decoder_1_out7;

  Decoder #(.select(3), .enable("false")) decoder_1 (
    .out1(decoder_1_out1), .out2(decoder_1_out2), .out3(decoder_1_out3), .out4(decoder_1_out4),
    .out5(decoder_1_out5), .out6(decoder_1_out6), .out7(decoder_1_out7), .sel(RW));  // open: out0
  and and_1 (and_1_out, decoder_1_out1, REG_write);
  and and_2 (and_2_out, decoder_1_out2, REG_write);
  and and_3 (and_3_out, decoder_1_out3, REG_write);
  and and_4 (and_4_out, decoder_1_out4, REG_write);
  and and_5 (and_5_out, decoder_1_out5, REG_write);
  and and_6 (and_6_out, decoder_1_out6, REG_write);
  and and_7 (and_7_out, decoder_1_out7, REG_write);
  Register #(.width(16)) R1 (.D(BUS_W), .en(and_1_out), .Q(out_15), .clk(Clock));  // open: clr
  Register #(.width(16)) R2 (.D(BUS_W), .en(and_2_out), .Q(out_14), .clk(Clock));  // open: clr
  Register #(.width(16)) R3 (.D(BUS_W), .en(and_3_out), .Q(out_13), .clk(Clock));  // open: clr
  Register #(.width(16)) R4 (.D(BUS_W), .en(and_4_out), .Q(out_12), .clk(Clock));  // open: clr
  Register #(.width(16)) R5 (.D(BUS_W), .en(and_5_out), .Q(out_11), .clk(Clock));  // open: clr
  Register #(.width(16)) R6 (.D(BUS_W), .en(and_6_out), .Q(out_10), .clk(Clock));  // open: clr
  Register #(.width(16)) R7 (.D(BUS_W), .en(and_7_out), .Q(out_9), .clk(Clock));  // open: clr
  Multiplexer #(.select(3), .width(16), .enable("false")) multiplexer_1 (
    .in0({16{1'b0}}), .in1(out_15), .in2(out_14), .in3(out_13), .in4(out_12), .in5(out_11), .in6(out_10),
    .in7(out_9), .out(BUS_A), .sel(RS));
  Multiplexer #(.select(3), .width(16), .enable("false")) multiplexer_2 (
    .in0({16{1'b0}}), .in1(out_15), .in2(out_14), .in3(out_13), .in4(out_12), .in5(out_11), .in6(out_10),
    .in7(out_9), .out(BUS_B), .sel(RT));

  assign out_16 = {16{1'b0}};

  // Other names for the same wires on the sheet: R1[15:0] = out_15; R2[15:0] = out_14; R3[15:0] = out_13;
  //   R4[15:0] = out_12; R5[15:0] = out_11; R6[15:0] = out_10; R7[15:0] = out_9

  // Notes on the sheet:
  //   R0
endmodule
