// Logisim project the main project.circ as structural Verilog: 5 circuits, main circuit main
// RegDst
module main (
  output out_1,
  output out_2
);

  wire Branch_Selc, Clock, I_type_Enable, MEM_Enable, MemRead, MemWrite, R_type_Enable, REG_write;
  wire [1:0] ALUSrc, Func, Jump_Selc, MemtoReg, RegDst;
  wire [2:0] Rd, Rs, Rt, RW;
  wire [3:0] Alu_Signal;
  wire [4:0] OP_code;
  wire [15:0] adder_2_out, adder_3_out, B, BUSA, BUSB, BUSW, LUI_result, multiplexer_2_out,
       multiplexer_3_out, O_P_of_RAM, PC, PC_1, register_file_1_out_9, register_file_1_out_10,
       register_file_1_out_11, register_file_1_out_12, register_file_1_out_13, register_file_1_out_14,
       register_file_1_out_15, register_file_1_out_16, Result_of_ALU, signed__Imm5, signed__Imm11,
       unsigned__Imm5;

  Clock clock_1 (.out(Clock));
  Register #(.width(16)) u_PC (.D(multiplexer_3_out), .Q(PC), .clk(Clock));  // open: en, clr
  Adder #(.width(16)) adder_1 (.a(16'h1), .b(PC), .out(PC_1));  // open: cin, cout
  Control_Unit control_unit_1 (
    .REG_write(REG_write), .Jump_Selc(Jump_Selc), .ALUSrc(ALUSrc), .Branch_Selc(Branch_Selc),
    .MemtoReg(MemtoReg), .MemWrite(MemWrite), .MemRead(MemRead), .RegDst(RegDst), .OP_Code(OP_code),
    .R_type_Enable(R_type_Enable), .I_type_Enable(I_type_Enable), .Zero_Flag(out_1),
    .Result_of_ALU(Result_of_ALU[0]), .MEM_Enable(MEM_Enable), .Func(Func));
  ROM #(.addrWidth(16), .dataWidth(16)) rom_1 (.addr(PC), .data({OP_code, Func, Rd, Rs, Rt}));  // open: sel
  Adder #(.width(16)) adder_2 (.a(PC), .b(signed__Imm5), .out(adder_2_out));  // open: cin, cout
  Multiplexer #(.select(2), .width(3), .enable("false")) multiplexer_1 (
    .in0(Rt), .in1(Rd), .in2(3'b001), .in3(3'b111), .out(RW), .sel(RegDst));
  assign signed__Imm11 = {{5{Func[1]}}, {Func, Rd, Rs, Rt}};  // Bit_Extender bit_extender_1
  assign signed__Imm5 = {{11{Func[1]}}, {Func, Rd}};  // Bit_Extender bit_extender_2
  assign unsigned__Imm5 = {{11{1'b0}}, {Func, Rd}};  // Bit_Extender bit_extender_3
  Multiplexer #(.width(16), .enable("false")) multiplexer_2 (
    .in0(PC_1), .in1(adder_2_out), .out(multiplexer_2_out), .sel(Branch_Selc));
  ALU_CONTROL alu_control_1 (
    .Selector_R_type({OP_code[0], Func}), .Enable1(R_type_Enable), .Selector_I_type(OP_code),
    .Enable2(I_type_Enable), .ALU_signal(Alu_Signal));
  // Probe on register_file_1_out_10
  // Probe on register_file_1_out_9
  Adder #(.width(16)) adder_3 (.a(PC), .b(signed__Imm11), .out(adder_3_out));  // open: cin, cout
  // Probe on register_file_1_out_11
  // Probe on register_file_1_out_12
  Register_file register_file_1 (
    .RW(RW), .REG_write(REG_write), .BUS_W(BUSW), .Clock(Clock), .BUS_A(BUSA), .RS(Rs), .BUS_B(BUSB),
    .RT(Rt), .out_16(register_file_1_out_16), .out_15(register_file_1_out_15),
    .out_14(register_file_1_out_14), .out_13(register_file_1_out_13), .out_12(register_file_1_out_12),
    .out_11(register_file_1_out_11), .out_10(register_file_1_out_10), .out_9(register_file_1_out_9));
  // Probe on register_file_1_out_14
  // Probe on register_file_1_out_13
  // Probe on register_file_1_out_16
  // Probe on register_file_1_out_15
  Multiplexer #(.select(2), .width(16), .enable("false")) multiplexer_3 (
    .in0(multiplexer_2_out), .in1(adder_3_out), .in2(BUSA), .out(multiplexer_3_out), .sel(Jump_Selc));  // open: in3
  Multiplexer #(.select(2), .width(16), .enable("false")) multiplexer_4 (
    .in0(BUSB), .in1(signed__Imm5), .in2(unsigned__Imm5), .out(B), .sel(ALUSrc));  // open: in3
  ALU alu_1 (.B(B), .A(BUSA), .ALU_signal(Alu_Signal), .ZERO_flag(out_1), .RESULT(Result_of_ALU), .Over_flow(out_2));
  Shifter #(.width(16)) shifter_1 (.in(signed__Imm11), .\dist (4'b0101), .out(LUI_result));
  RAM #(.addrWidth(16), .dataWidth(16), .bus("separate")) ram_1 (
    .addr(Result_of_ALU), .din(BUSB), .data(O_P_of_RAM), .str(MemWrite), .sel(MEM_Enable), .clk(Clock),
    .ld(MemRead));  // open: clr
  Multiplexer #(.select(2), .width(16), .enable("false")) multiplexer_5 (
    .in0(Result_of_ALU), .in1(O_P_of_RAM), .in2(PC_1), .in3(LUI_result), .out(BUSW), .sel(MemtoReg));

  // Other names for the same wires on the sheet: Over_Flow = out_2; ZERO_Flag = out_1

  // Notes on the sheet:
  //   first bit
  //   contents of rom_1 (hex, n*v repeats v):
  //   3941 492 3883 6813 405b 3fc9 3852 7f08 3941 f803 968 7000 6026 96e 3864 8761 1038
  //   Circuit of Control Unit And Alu_Signal
  //   IMM10 0:10
  //   IMM5 6:10
  //   IMM5 6:10
  //   3:5 Rs
  //   0:2 Rt
  //   6:8 Rd
  //   OP code 11:15
  //   Func 9&10
  //   Branches
  //   FT and first bit
  //   of OP code
  //   Circuit of PC
  //   for J and JAL
  //   Content of registers
  //   for JR
  //   BY :  Abanob Evram
  //   Mina Moawad
  //   Mark Amgad
  //   Department of electronics and communication
  //   Circuit of LUI
  //   for JAL
endmodule

module Register_file (
  input  [2:0] RS,
  input  [2:0] RW,
  input  [2:0] RT,
  input  REG_write,
  input  [15:0] BUS_W,
  input  Clock,
  output [15:0] BUS_A,
  output [15:0] BUS_B,
  output [15:0] out_9,
  output [15:0] out_10,
  output [15:0] out_11,
  output [15:0] out_12,
  output [15:0] out_13,
  output [15:0] out_14,
  output [15:0] out_15,
  output [15:0] out_16
);

  wire and_1_out, and_2_out, and_3_out, and_4_out, and_5_out, and_6_out, and_7_out, decoder_1_out1,
       decoder_1_out2, decoder_1_out3, decoder_1_out4, decoder_1_out5, decoder_1_out6, decoder_1_out7;

  Decoder #(.select(3), .enable("false")) decoder_1 (
    .out1(decoder_1_out1), .out2(decoder_1_out2), .out3(decoder_1_out3), .out4(decoder_1_out4),
    .out5(decoder_1_out5), .out6(decoder_1_out6), .out7(decoder_1_out7), .sel(RW));  // open: out0
  and and_1 (and_1_out, decoder_1_out1, REG_write);
  and and_2 (and_2_out, decoder_1_out2, REG_write);
  and and_3 (and_3_out, decoder_1_out3, REG_write);
  and and_4 (and_4_out, decoder_1_out4, REG_write);
  and and_5 (and_5_out, decoder_1_out5, REG_write);
  and and_6 (and_6_out, decoder_1_out6, REG_write);
  and and_7 (and_7_out, decoder_1_out7, REG_write);
  Register #(.width(16)) R1 (.D(BUS_W), .en(and_1_out), .Q(out_15), .clk(Clock));  // open: clr
  Register #(.width(16)) R2 (.D(BUS_W), .en(and_2_out), .Q(out_14), .clk(Clock));  // open: clr
  Register #(.width(16)) R3 (.D(BUS_W), .en(and_3_out), .Q(out_13), .clk(Clock));  // open: clr
  Register #(.width(16)) R4 (.D(BUS_W), .en(and_4_out), .Q(out_12), .clk(Clock));  // open: clr
  Register #(.width(16)) R5 (.D(BUS_W), .en(and_5_out), .Q(out_11), .clk(Clock));  // open: clr
  Register #(.width(16)) R6 (.D(BUS_W), .en(and_6_out), .Q(out_10), .clk(Clock));  // open: clr
  Register #(.width(16)) R7 (.D(BUS_W), .en(and_7_out), .Q(out_9), .clk(Clock));  // open: clr
  Multiplexer #(.select(3), .width(16), .enable("false")) multiplexer_1 (
    .in0({16{1'b0}}), .in1(out_15), .in2(out_14), .in3(out_13), .in4(out_12), .in5(out_11), .in6(out_10),
    .in7(out_9), .out(BUS_A), .sel(RS));
  Multiplexer #(.select(3), .width(16), .enable("false")) multiplexer_2 (
    .in0({16{1'b0}}), .in1(out_15), .in2(out_14), .in3(out_13), .in4(out_12), .in5(out_11), .in6(out_10),
    .in7(out_9), .out(BUS_B), .sel(RT));

  assign out_16 = {16{1'b0}};

  // Other names for the same wires on the sheet: R1[15:0] = out_15; R2[15:0] = out_14; R3[15:0] = out_13;
  //   R4[15:0] = out_12; R5[15:0] = out_11; R6[15:0] = out_10; R7[15:0] = out_9

  // Notes on the sheet:
  //   R0
endmodule

module ALU (
  input  [15:0] B,
  input  [15:0] A,
  input  [3:0] ALU_signal,
  output ZERO_flag,
  output [15:0] RESULT,
  output Over_flow
);

  wire adder_1_cout, comparator_1_lt, comparator_2_eq, comparator_2_gt, comparator_2_lt, not_2_out, or_2_out,
       subtractor_1_bout, xor_2_out, xor_3_out;
  wire [15:0] adder_1_out, and_1_out, bit_extender_1_out, bit_extender_2_out, bit_extender_3_out,
       bit_extender_4_out, bit_extender_5_out, bit_extender_6_out, not_1_out, or_1_out, shifter_1_out,
       shifter_2_out, shifter_3_out, shifter_4_out, subtractor_1_out, xor_1_out;

  Comparator #(.width(16), .mode("unsigned")) comparator_1 (.a(A), .b(B), .lt(comparator_1_lt));  // open: gt, eq
  Comparator #(.width(16)) comparator_2 (
    .a(A), .b(B), .gt(comparator_2_gt), .eq(comparator_2_eq), .lt(comparator_2_lt));
  assign and_1_out = A & B;  // AND_Gate and_1, 16 bits wide
  assign or_1_out = A | B;  // OR_Gate or_1, 16 bits wide
  assign xor_1_out = A ^ B;  // XOR_Gate xor_1, 16 bits wide
  Adder #(.width(16)) adder_1 (.a(A), .b(B), .out(adder_1_out), .cout(adder_1_cout));  // open: cin
  Subtractor #(.width(16)) subtractor_1 (.a(A), .b(B), .out(subtractor_1_out), .bout(subtractor_1_bout));  // open: bin
  assign not_1_out = ~or_1_out;  // NOT_Gate not_1, 16 bits wide
  not not_2 (not_2_out, comparator_2_eq);
  or or_2 (or_2_out, comparator_2_eq, comparator_2_gt);
  Comparator #(.width(16)) comparator_3 (.a(A), .b(B), .eq(ZERO_flag));  // open: gt, lt
  Shifter #(.width(16)) shifter_1 (.in(A), .\dist (B[3:0]), .out(shifter_1_out));
  Shifter #(.width(16), .shift("lr")) shifter_2 (.in(A), .\dist (B[3:0]), .out(shifter_2_out));
  Shifter #(.width(16), .shift("ar")) shifter_3 (.in(A), .\dist (B[3:0]), .out(shifter_3_out));
  Shifter #(.width(16), .shift("rr")) shifter_4 (.in(A), .\dist (B[3:0]), .out(shifter_4_out));
  xor xor_2 (xor_2_out, adder_1_out[15], adder_1_cout);
  xor xor_3 (xor_3_out, subtractor_1_out[15], subtractor_1_bout);
  assign bit_extender_1_out = {{15{1'b0}}, comparator_2_eq};  // Bit_Extender bit_extender_1
  assign bit_extender_2_out = {{15{1'b0}}, not_2_out};  // Bit_Extender bit_extender_2
  assign bit_extender_3_out = {{15{1'b0}}, comparator_2_lt};  // Bit_Extender bit_extender_3
  assign bit_extender_4_out = {{15{1'b0}}, or_2_out};  // Bit_Extender bit_extender_4
  or or_3 (Over_flow, xor_2_out, xor_3_out);
  assign bit_extender_5_out = {{15{1'b0}}, comparator_2_lt};  // Bit_Extender bit_extender_5
  assign bit_extender_6_out = {{15{1'b0}}, comparator_1_lt};  // Bit_Extender bit_extender_6
  Multiplexer #(.select(4), .width(16), .enable("false")) multiplexer_1 (
    .in0(shifter_1_out), .in1(shifter_2_out), .in2(shifter_3_out), .in3(shifter_4_out), .in4(and_1_out),
    .in5(not_1_out), .in6(or_1_out), .in7(xor_1_out), .in8(adder_1_out), .in9(subtractor_1_out),
    .in10(bit_extender_5_out), .in11(bit_extender_6_out), .in12(bit_extender_1_out),
    .in13(bit_extender_2_out), .in14(bit_extender_3_out), .in15(bit_extender_4_out), .out(RESULT),
    .sel(ALU_signal));

  // Notes on the sheet:
  //   First comparator : for check SLTU
  //   Second comparator :for check SLT,BEQ,BLT,BGE
  //   Shift amont 0:4
  //   SLL 0
  //   SRL 1
  //   SRA 2
  //   ROR 3
  //   AND 4
  //   NOR 5
  //   OR 6
  //   XOR 7
  //   ADD 8
  //   SUB 9
  //   SLT 10
  //   SLTU11
  //   BEQ 12
  //   BNE 13
  //   BLT 14
  //   BGE 15
endmodule

// ALU_Signal
module ALU_CONTROL (
  input  [2:0] Selector_R_type,
  input  Enable1,
  input  [4:0] Selector_I_type,
  input  Enable2,
  output [3:0] ALU_signal
);

  wire [3:0] multiplexer_1_out, multiplexer_2_out;

  Multiplexer #(.select(3), .width(4)) multiplexer_1 (
    .in0(4'b0100), .in1(4'b0110), .in2(4'b0111), .in3(4'b0101), .in4(4'b1000), .in5(4'b1001), .in6(4'b1010),
    .in7(4'b1011), .out(multiplexer_1_out), .sel(Selector_R_type), .en(Enable1));
  Multiplexer #(.select(5), .width(4)) multiplexer_2 (
    .in4(4'b0100), .in5(4'b0110), .in6(4'b0111), .in7(4'b1000), .in8(4'b0000), .in9(4'b0001), .in10(4'b0010),
    .in11(4'b0011), .in12(4'b1000), .in13(4'b1000), .in14(4'b1100), .in15(4'b1101), .in16(4'b1110),
    .in17(4'b1111), .out(multiplexer_2_out), .sel(Selector_I_type), .en(Enable2));  // open: in0, in1, in2, in3, in18, in19, in20, in21, in22, in23, in24, in25, in26, in27, in28, in29, in30, in31
  Multiplexer #(.width(4), .enable("false")) multiplexer_3 (
    .in0(multiplexer_1_out), .in1(multiplexer_2_out), .out(ALU_signal), .sel(Enable2));

  // Notes on the sheet:
  //   First MUX
  //   Second MUX
  //   R_TYPE
  //   I_Type
  //   if the enable of the second mux is 0 then the second mux is disabled and the main mux selector is 0 which is the first mux output
  //   Main MUX
endmodule

module Control_Unit (
  input  Zero_Flag,
  input  Result_of_ALU,
  input  [1:0] Func,
  input  [4:0] OP_Code,
  output REG_write,
  output [1:0] Jump_Selc,
  output [1:0] ALUSrc,
  output MemWrite,
  output MemRead,
  output Branch_Selc,
  output MEM_Enable,
  output R_type_Enable,
  output [1:0] MemtoReg,
  output [1:0] RegDst,
  output I_type_Enable
);

  wire AddI, and_2_out, and_3_out, and_4_out, and_5_out, ANDI, BEQ, BGE, BLT, BNE, decoder_1_out0,
       decoder_1_out1, J, JAL, JR, LUI, not_1_out, not_2_out, not_3_out, ORI, priority_encoder_1_p2,
       priority_encoder_2_p2, priority_encoder_2_p3, priority_encoder_2_p4, priority_encoder_3_p2,
       priority_encoder_3_p3, priority_encoder_3_p4, priority_encoder_4_p2, ROR, SLL, SRA, SRL, XORI;

  Decoder #(.select(5), .enable("false")) decoder_1 (
    .out0(decoder_1_out0), .out1(decoder_1_out1), .out2(JR), .out4(ANDI), .out5(ORI), .out6(XORI),
    .out7(AddI), .out8(SLL), .out9(SRL), .out10(SRA), .out11(ROR), .out12(MemRead), .out13(MemWrite),
    .out14(BEQ), .out15(BNE), .out16(BLT), .out17(BGE), .out18(LUI), .out30(J), .out31(JAL), .sel(OP_Code));  // open: out3, out19, out20, out21, out22, out23, out24, out25, out26, out27, out28, out29
  or or_1 (MEM_Enable, MemWrite, MemRead);
  or or_2 (I_type_Enable, MemRead, ANDI, ORI, XORI, AddI, SLL, SRL, SRA, ROR, BEQ, BNE, BLT, BGE, MemWrite);
  or or_3 (R_type_Enable, decoder_1_out0, decoder_1_out1);
  or or_4 (REG_write, SLL, R_type_Enable, ANDI, ORI, XORI, AddI, SRL, SRA, ROR, MemRead, JAL, LUI);
  // Priority_Encoder #(.select(2)) priority_encoder_1: pin names not known; wires that end beside it: RegDst, priority_encoder_1_p2, R_type_Enable, LUI, JAL
  // Priority_Encoder #(.select(2)) priority_encoder_2: pin names not known; wires that end beside it: ALUSrc, priority_encoder_2_p2, priority_encoder_2_p3, priority_encoder_2_p4
  or or_5 (priority_encoder_2_p4, ANDI, ORI, XORI, SLL, SRL, SRA, ROR);
  or or_6 (priority_encoder_1_p2, ANDI, ORI, XORI, AddI, SLL, SRL, SRA, ROR, MemRead);
  or or_7 (priority_encoder_2_p2, R_type_Enable, BEQ, BNE, BLT, BGE);
  or or_8 (priority_encoder_2_p3, AddI, MemRead, MemWrite);
  or or_9 (Branch_Selc, and_2_out, and_3_out, and_4_out, and_5_out);
  // Priority_Encoder #(.select(2)) priority_encoder_3: pin names not known; wires that end beside it: Jump_Selc, priority_encoder_3_p2, priority_encoder_3_p3, priority_encoder_3_p4
  // Priority_Encoder #(.select(2)) priority_encoder_4: pin names not known; wires that end beside it: MemtoReg, priority_encoder_4_p2, MemRead, JAL, LUI
  or or_10 (priority_encoder_3_p2, R_type_Enable, ANDI, ORI, XORI, AddI, SLL, SRL, SRA, ROR, MemRead, MemWrite, BEQ, BNE, BLT, BGE, LUI);
  or or_11 (priority_encoder_3_p3, J, JAL);
  and and_1 (priority_encoder_3_p4, JR, not_1_out, not_2_out);
  and and_2 (and_2_out, BEQ, Zero_Flag);
  and and_3 (and_3_out, BNE, not_3_out);
  and and_4 (and_4_out, BLT, Result_of_ALU);
  and and_5 (and_5_out, BGE, Result_of_ALU);
  or or_12 (priority_encoder_4_p2, R_type_Enable, ANDI, ORI, XORI, AddI, SLL, SRL, SRA, ROR);
  not not_1 (not_1_out, Func[0]);
  not not_2 (not_2_out, Func[1]);
  not not_3 (not_3_out, Zero_Flag);

  // Other names for the same wires on the sheet: LW = MemRead; R_Type = R_type_Enable; SW = MemWrite

  // Notes on the sheet:
  //   Enable for ALU Control Unit
  //   if 0 Rt is slected
  //      1 Rd is sleced
  //     2 R1 is slected
  //   3 R7 is slected
  //   allow to write
  //     1 signed (Imm5)
  //   if 1 REG write is Enable
  //   if 0 BUSB  is activated
  //   2 unsigned (Imm5)
  //   3 to LUI
  //   0 to  ALU Operations
  //   1 to select load 
  //   2 to select JAL
  //   0 for branches or PC+1
  //   1 for J and JAL
  //   2 for JR
endmodule
